# Fritzing sketch quickdraw_circuit (saved by Fritzing 0.9.3b)
breadboards: 2
stripboards: 1

parts:
  Raspberry_Pi_1 = Raspberry Pi 3 [part_number=RPI-3-V1.2]
  IC1 = MCP3008 8-channel 10-bit ADC [part_number=MCP3008]
  J4 = Screw terminal - 2 pins [package=THT]
  J5 = Screw terminal - 2 pins [package=THT]
  J6 = Piezo Speaker
  U1 = attiny85 [package=dip]
  R9 = Resistor [tolerance=±5% resistance=1M package=THT]
  J7 = Screw terminal - 2 pins [package=THT]
  J8 = Screw terminal - 2 pins [package=THT]
  J9 = Screw terminal - 2 pins [package=THT]
  J11 = Screw terminal - 2 pins [package=THT]
  DOTSTAR1 = DotStar Strip -- Black (60/m) [part_number=2239]
  PART1 = Tiny AVR Programmer [part_number=PGM-11801]  # not connected
  S1 = Toggle Switch [package=THT]
  S2 = Toggle Switch [package=THT]
  J12 = Screw terminal - 2 pins [package=THT]

nets:
  N1: Raspberry_Pi_1.3V3, Raspberry_Pi_1.GPIO10, IC1.no_name_yet#11
  N2: Raspberry_Pi_1.GPIO9, IC1.no_name_yet#12
  N3: Raspberry_Pi_1.GPIO11, IC1.no_name_yet#13
  N4: Raspberry_Pi_1.GPIO8, IC1.no_name_yet#10
  N5: Raspberry_Pi_1.GND, IC1.no_name_yet#9, IC1.no_name_yet#14
  N6: Raspberry_Pi_1.5V, IC1.no_name_yet#15, IC1.no_name_yet#16, S1.L1
  N7: IC1.no_name_yet#1, J5.pin1
  N8: IC1.no_name_yet#2, J5.pin2
  N9: IC1.no_name_yet#3, J7.pin1
  N10: IC1.no_name_yet#4, J7.pin2
  N11: IC1.no_name_yet#5, J8.pin1
  N12: IC1.no_name_yet#6, J8.pin2
  N13: IC1.no_name_yet#7, J9.pin1, S2.COM
  N14: IC1.no_name_yet#8, J9.pin2
  N15: J4.pin1, U1.Pin_1
  N16: J4.pin2, U1.Pin_2, DOTSTAR1.DI
  N17: J6.pin1, U1.Pin_4, R9.Pin_0, J11.pin2, DOTSTAR1.GND, J12.pin2
  N18: J6.pin2, U1.Pin_7, R9.Pin_1, J12.pin1
  N19: U1.Pin_3, J11.pin1, DOTSTAR1.CI
  N20: S1.COM, S2.L1

custom parts:
  DotStar Strip -- Black (60/m): NeopixelDotStar Strip, Black, 60 pixels per meter.
  Tiny AVR Programmer: The ATtiny45 and 85 are a couple of really cool little MCUs but did you know you can program them in Arduino? That’s right, now you can shrink your Arduino projects down to “tiny size” by moving your code straight over to these small but capable ICs. The standard method for programming the ATtiny ICs involves a breadboard, lots of jumper wires and a hardware programmer, but David Mellis over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
